# Fritzing sketch Untitled Sketch (saved by Fritzing 0.9.3b)

parts:
  元件1 = Arduino Uno (Rev3)
  PIR = IR Receiver Breakout [package=PCB]
  红外信号发射端 = TSOP312.., 314.. [package=THT]  # not connected

nets:
  N1: 元件1.D13/SCK, PIR.OUT
  5V: 元件1.5V, PIR.VCC
  GND: 元件1.GND, PIR.GND
